// Digital circuit Address register.dig as structural Verilog
module Address_register (
  input  in_5,
  input  in_6,
  input  in_7,
  input  in_8,
  input  in_9,
  input  in_10,
  input  in_11,
  input  in_12,
  output out_1,
  output out_2,
  output out_3,
  output out_4
);

  wire _7408_1_pin1, _7408_1_pin3, _7408_1_pin4, _7408_1_pin6, _7408_1_pin8, _7408_1_pin9, _7408_1_pin11,
       _7408_1_pin12, _7432_1_pin1, _7432_1_pin4, _7432_1_pin9, _7432_1_pin12, _74173_1_pin11,
       _74173_1_pin12, _74173_1_pin13, _74173_1_pin14;

  _7408 _7408_1 (
    .pin1(_7408_1_pin1), .pin2(in_8), .pin3(_7408_1_pin3), .pin4(_7408_1_pin4), .pin5(in_8),
    .pin6(_7408_1_pin6), .pin7(1'b0), .pin8(_7408_1_pin8), .pin9(_7408_1_pin9), .pin10(in_8),
    .pin11(_7408_1_pin11), .pin12(_7408_1_pin12), .pin13(in_8), .pin14(1'b1));
  _74283 _74283_1 (
    .pin1(_7408_1_pin4), .pin2(1'b0), .pin3(out_2), .pin4(_7408_1_pin1), .pin5(out_1), .pin6(1'b1),
    .pin7(1'b0), .pin8(1'b0), .pin10(_7408_1_pin12), .pin11(1'b0), .pin12(out_4), .pin13(_7408_1_pin9),
    .pin14(out_3), .pin15(1'b0), .pin16(1'b1));  // open: pin9
  _74173 _74173_1 (
    .pin1(1'b0), .pin2(1'b0), .pin3(out_4), .pin4(out_3), .pin5(out_2), .pin6(out_1), .pin7(in_7),
    .pin8(1'b0), .pin9(1'b0), .pin10(1'b0), .pin11(_74173_1_pin11), .pin12(_74173_1_pin12),
    .pin13(_74173_1_pin13), .pin14(_74173_1_pin14), .pin15(in_5), .pin16(1'b1));
  _7432 _7432_1 (
    .pin1(_7432_1_pin1), .pin2(_7408_1_pin3), .pin3(_74173_1_pin14), .pin4(_7432_1_pin4),
    .pin5(_7408_1_pin6), .pin6(_74173_1_pin13), .pin7(1'b0), .pin8(_74173_1_pin12), .pin9(_7432_1_pin9),
    .pin10(_7408_1_pin8), .pin11(_74173_1_pin11), .pin12(_7432_1_pin12), .pin13(_7408_1_pin11), .pin14(1'b1));
  _7408 _7408_2 (
    .pin1(in_12), .pin2(in_6), .pin3(_7432_1_pin1), .pin4(in_11), .pin5(in_6), .pin6(_7432_1_pin4),
    .pin7(1'b0), .pin8(_7432_1_pin9), .pin9(in_10), .pin10(in_6), .pin11(_7432_1_pin12), .pin12(in_9),
    .pin13(in_6), .pin14(1'b1));
endmodule
