// Digital circuit Registers and Programmer.dig as structural Verilog
module Registers_and_Programmer (
  input  in_1,
  input  in_2,
  input  in_3,
  input  in_12,
  input  in_13,
  input  in_14,
  input  in_15,
  input  in_16,
  input  in_17,
  input  in_18,
  input  in_19,
  input  in_20,
  input  in_21,
  output out_4,
  output out_5,
  output out_6,
  output out_7,
  output out_8,
  output out_9,
  output out_10,
  output out_11
);

  wire _7404_1_pin8, _7404_1_pin10;

  _7404 _7404_1 (
    .pin1(1'b0), .pin3(1'b0), .pin5(1'b0), .pin7(1'b0), .pin8(_7404_1_pin8), .pin9(in_2),
    .pin10(_7404_1_pin10), .pin11(in_21), .pin13(1'b0), .pin14(1'b1));  // open: pin2, pin4, pin6, pin12
  _74173 _74173_1 (
    .pin1(in_3), .pin2(in_3), .pin3(out_4), .pin4(out_5), .pin5(out_6), .pin6(out_7), .pin7(in_1),
    .pin8(1'b0), .pin9(_7404_1_pin8), .pin10(_7404_1_pin8), .pin11(in_20), .pin12(in_19), .pin13(in_18),
    .pin14(in_17), .pin15(in_12), .pin16(1'b1));
  // Adapted_28C16A adapted_28c16a_1: pin names not known; wires that end beside it: 1'b1, 1'b0, 1'b0, 1'b0, 1'b0, 1'b0, 1'b0, 1'b0, 1'b1, in_13, 1'b0, in_14, in_3, in_15, out_4, in_16, out_5, out_11, out_6, out_10, out_9, 1'b0
  _74173 _74173_2 (
    .pin1(in_3), .pin2(in_3), .pin3(out_8), .pin4(out_9), .pin5(out_10), .pin6(out_11), .pin7(in_1),
    .pin8(1'b0), .pin9(_7404_1_pin10), .pin10(_7404_1_pin10), .pin11(in_20), .pin12(in_19), .pin13(in_18),
    .pin14(in_17), .pin15(in_12), .pin16(1'b1));
endmodule
