// Digital circuit register.dig as structural Verilog
module register (
  input  in_5,
  input  in_6,
  input  in_7,
  input  in_8,
  input  in_9,
  input  in_10,
  input  in_11,
  output out_1,
  output out_2,
  output out_3,
  output out_4
);

  wire _74173_1_pin9;

  _74173 _74173_1 (
    .pin1(1'b0), .pin2(1'b0), .pin3(out_1), .pin4(out_2), .pin5(out_3), .pin6(out_4), .pin7(in_11),
    .pin8(1'b0), .pin9(_74173_1_pin9), .pin10(_74173_1_pin9), .pin11(in_8), .pin12(in_7), .pin13(in_6),
    .pin14(in_5), .pin15(in_9), .pin16(1'b1));
  LED led_1 (.in(out_1));
  LED led_2 (.in(out_2));
  LED led_3 (.in(out_3));
  LED led_4 (.in(out_4));
  _7404 _7404_1 (
    .pin1(1'b0), .pin3(1'b0), .pin5(1'b0), .pin7(1'b0), .pin8(_74173_1_pin9), .pin9(in_10), .pin11(1'b0),
    .pin13(1'b0), .pin14(1'b1));  // open: pin2, pin4, pin6, pin10, pin12
endmodule
